# Fritzing sketch HelloMCP3008 (saved by Fritzing 0.9.9b)
breadboards: 1

parts:
  Mod1 = Raspberry Pi 4B
  ADC1 = MCP3008 [package=dil16]
  R1 = Rotary Potentiometer (Small) [maximum_resistance=100kΩ package=THT]

nets:
  3V3: Mod1.3V3, ADC1.VREF, ADC1.VDD, R1.leg2
  N1: Mod1.GND, ADC1.DGND, ADC1.AGND, R1.leg1
  N2: Mod1.GPIO10, ADC1.Din
  N3: Mod1.GPIO9, ADC1.Dout
  N4: Mod1.GPIO11, ADC1.CLK
  N5: Mod1.GPIO8, ADC1.CS/SHDN
  N6: ADC1.CH0, R1.wiper
